# Fritzing sketch main (saved by Fritzing 0.9.6b)

parts:
  Yumo-enc1 = YumoE6B2
  Yumo-enc2 = YumoE6B2
  BeagleBone1 = BeagleBone Black
  L298N1 = L298N DC motor driver
  BATT1 = LiPoly Battery (1300mAh)
  M1 = DC Motor
  M2 = DC Motor

nets:
  N1: Yumo-enc1.V, BeagleBone1.no_name_yet#5
  N2: Yumo-enc1.A, BeagleBone1.no_name_yet#27
  N3: Yumo-enc1.B, BeagleBone1.no_name_yet#42
  N4: Yumo-enc1.GND, BeagleBone1.no_name_yet#1
  N5: Yumo-enc2.V, BeagleBone1.no_name_yet#6
  N6: Yumo-enc2.A, BeagleBone1.no_name_yet#111
  N7: Yumo-enc2.B, BeagleBone1.no_name_yet#112
  N8: Yumo-enc2.GND, BeagleBone1.no_name_yet#102
  N9: BeagleBone1.no_name_yet#2, L298N1.GND, BATT1.negative
  N10: BeagleBone1.no_name_yet#14, L298N1.ENA
  N11: BeagleBone1.no_name_yet#16, L298N1.ENB
  N12: BeagleBone1.no_name_yet#107, L298N1.IN1
  N13: BeagleBone1.no_name_yet#108, L298N1.IN2
  N14: BeagleBone1.no_name_yet#109, L298N1.IN3
  N15: BeagleBone1.no_name_yet#110, L298N1.IN4
  N16: L298N1.OUT1, M2.pin_2
  N17: L298N1.OUT2, M2.pin_1
  N18: L298N1.OUT3, M1.pin_2
  N19: L298N1.OUT4, M1.pin_1
  N20: L298N1.12V, BATT1.positive

custom parts:
  BeagleBone Black: BeagleBone Black rev. A5B
  L298N DC motor driver: 2x DC motor driver with 78M05 positive voltage regulator (7..35 V) L298N: max 46 V, 2 A Set 5 V Enable jumper to enable 5 V regultor (needed for the L298N) and +5 V output at screw terminal or supply external +5 V at screw terminal Set ENA and/or ENB to +5 V to enable motor permanently or supply ENA and/or ENB with PWM signal IN1 and IN2 set rotation directory for motor A (OUT1/OUT2) IN2 and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
  LiPoly Battery (1300mAh): Lithium Ion Polymer Battery (1300mAh)
